# Fritzing sketch Circuit_diagram_morse_code_decorder_v1 (saved by Fritzing 0.9.3b)

parts:
  LCD1 = LCD screen
  Part1 = Arduino Pro Mini v13
  LED1 = smd LED [color="Red (633nm)" package="0603 [SMD]"]
  J1 = Piezo Speaker
  R2 = Resistor [tolerance=±5% resistance=10 package=THT]

nets:
  VSS: LCD1.VSS, LCD1.R/W, Part1.GND, LED1.cathode, J1.pin1, R2.Pin_0
  VDD: LCD1.VDD, Part1.VCC
  N1: LCD1.V0, R2.Pin_1
  N2: LCD1.RS, Part1.D12/MISO
  N3: LCD1.E, Part1.D11_PWM/MOSI
  N4: LCD1.DB4, Part1.D5_PWM
  N5: LCD1.DB5, Part1.D4
  N6: LCD1.DB6, Part1.D3_PWM
  N7: LCD1.DB7, Part1.D2
  N8: Part1.D13/SCK, LED1.anode
  N9: Part1.D8, J1.pin2
